# Fritzing sketch extruder (saved by Fritzing 0.9.3b)

parts:
  LED1 = LED - 3mm [color="Red (633nm)" package="3 mm [THT]"]
  LED2 = LED - 3mm [color="Green (555nm)" package="3 mm [THT]"]
  M1 = Stepper Motor - Bipolar
  M2 = Stepper Motor - Bipolar
  U1 = SWITCH-SPST-2 [package=switch-spst-vertical]
  U3 = SWITCH-SPST-2 [package=switch-spst-vertical]
  S4 = Pushbutton [package="[SMD]"]
  S5 = SWITCH-SPST-2 [package=r_sw_th]
  R1 = Resistor [tolerance=±5% resistance=0 package="0805 [SMD]"]
  OMRON2 = OMRON PCB Power Relay – G5LE [part_number="G5LE-1\n" package=THT]
  JACK1 = 2.1mm Barrel Jack with Terminal Block
  Part4 = EasyDriver_v44
  Part5 = EasyDriver_v44
  Part3 = Arduino Mega 2560 (Rev3)
  U6 = SWITCH-SPST-2 [package=switch-spst-vertical]
  U7 = SWITCH-SPST-2 [package=switch-spst-vertical]
  U8 = SWITCH-SPST-2 [package=switch-spst-vertical]
  U9 = SWITCH-SPST-2 [package=switch-spst-vertical]
  U10 = SWITCH-SPST-2 [package=switch-spst-vertical]
  OMRON4 = OMRON PCB Power Relay – G5LE [part_number="G5LE-1\n" package=THT]
  OMRON5 = OMRON PCB Power Relay – G5LE [part_number="G5LE-1\n" package=THT]
  F1 = Fan - Ventilador [package=THT]
  F4 = Fan - Ventilador [package=THT]
  LCD1 = LCD screen
  R4 = Trimmer Potentiometer [maximum_resistance=10kΩ package=THT]
  R5 = Resistor [tolerance=±5% resistance=220 package="2512 [SMD]"]
  S6 = SWITCH-SPST-2 [package=r_sw_th]
  R2 = Temperature Sensor (Thermistor) [thermistor_type=NTC package=THT]
  U11 = MAX6675 [package=so08]
  R6 = Resistor [tolerance=±5% resistance=47k package=THT]
  JACK3 = 2.1mm Barrel Jack with Terminal Block  # not connected
  HLK-PM1 = HLK-PM01

nets:
  N1: LED1.cathode, Part3.D8_PWM
  GND: LED1.anode, LED2.anode, U1.P, U3.P, S4.Pin_1, S4.Pin_2, OMRON2.COIL1, Part4.GND, Part5.GND, Part3.GND, U6.P, U7.P, U8.P, U9.P, U10.P, OMRON4.COIL2, OMRON4.B, OMRON5.COIL2, OMRON5.B, LCD1.VSS, LCD1.R/W, LCD1.LED-, R4.leg1, U11.VSS, R6.Pin_1, HLK-PM1.-Vo
  N2: LED2.cathode, Part3.D9_PWM
  N3: M1.A, Part4.OUT2A
  N4: M1.C, Part4.OUT2B
  N5: M1.B, Part4.OUT1A
  N6: M1.D, Part4.OUT1B
  N7: M2.A, Part5.OUT2A
  N8: M2.C, Part5.OUT2B
  N9: M2.B, Part5.OUT1A
  N10: M2.D, Part5.OUT1B
  N11: U1.O, Part3.D15/RX3
  N12: U3.O, Part3.D14/TX3
  N13: S4.Pin_4, Part3.D27
  N14: S5.O, JACK1.NEG
  N15: S5.P, S6.O
  N16: R1.Pin_0, OMRON2.B
  N17: R1.Pin_1, JACK1.POS, HLK-PM1.AC#1
  N18: OMRON2.C, S6.P, HLK-PM1.AC#0
  N19: OMRON2.COIL2, Part3.D26
  5V: Part4.V+, Part5.V+, F1.5V, F4.5V, HLK-PM1.+Vo
  N20: Part4.STEP, Part3.D6_PWM
  N21: Part4.DIR, Part3.D5_PWM
  VCC: Part4.VCC, Part5.VCC, Part3.5V, LCD1.VDD, R4.leg2, R5.Pin_1, U11.VDD
  N22: Part4.ENABLE, Part3.D7_PWM
  N23: Part5.STEP, Part3.D3_PWM
  N24: Part5.DIR, Part3.D2_PWM
  N25: Part5.ENABLE, Part3.D4_PWM
  N26: Part3.D21/SCL, OMRON5.COIL1
  N27: Part3.D20/SDA, U10.O
  N28: Part3.D19/RX1, U9.O
  N29: Part3.D18/TX1, U8.O
  N30: Part3.D17_PWM/RX2, U7.O
  N31: Part3.D16_PWM/TX2, U6.O
  N32: Part3.D12_PWM, U11.SCK
  N33: Part3.D11_PWM, U11.CS
  N34: Part3.D10_PWM, U11.MISO
  N35: Part3.D23, OMRON4.COIL1
  N36: Part3.D45, LCD1.DB7
  N37: Part3.D47, LCD1.DB6
  N38: Part3.D49, LCD1.DB5
  N39: Part3.D51, LCD1.DB3, LCD1.DB4
  N40: Part3.D52, LCD1.RS
  N41: Part3.D53, LCD1.E
  N42: OMRON4.C, F4.GND
  N43: OMRON5.C, F1.GND
  N44: LCD1.V0, R4.wiper
  N45: LCD1.LED+, R5.Pin_0
  N46: R2.pin_0, U11.T+, R6.Pin_0
  N47: R2.pin_1, U11.T-

notes:
  Indicadors temperatura calent/fred
  Placa base Arduino Mega 2650
  Motor de passos: extrusor
  Motor de passos: bobina
  Interruptor diferencials automàtic i magnetotèrmic
  Controladores motors
  tb6600
  Relé d'Estat Sòlid per la resistència
  Resistènica per escalfar
  NTC + MAX6675k
  Adaptador corrent AC 230V
  Int: invertir direcció bobina
  Int: invertir direcció extrusora
  Int: rotar bobina
  Int: extrudir
  Int: escalfar
  Int: ventilador controladores i arduino
  Int: ventilador filament i bobina
  STOP
  Relé vent. filament i bobina
  ventilador filament i bobina
  Ventilador controladores i Arduino
  LCD 16x2caràcters (16pins)
  Selector de contrast
  D13: LED operacions
  font d'alimentació 230V AC a 12V DC
  Relé vent. controladores i Arduino
  Font d'alimentació 5V DC
  Colors dels cablse:
  Blau: Digital enviar
  Blanc: Digital rebre
  Groc: Digital enviar/rebre commutat
  Vermell: +5V
  Negre: -5V
  Lila: +12V
  Marró: -12V
  Rosa: +230V
  Gris: -230V
  Verd: Terra
  Connectors Terra repartits per la base metàlica

custom parts:
  Fan - Ventilador: Ventilador de 2 pines, se encuentra comunmente en computadoras de escritorio
  HLK-PM01: AC-DC 220V to 12V Step-Down Power Supply Module

// code stored in the sketch: .ino
/*

  Extrusora de PLA controlada per Arduino Mega 2560.

  Projecte: 
  - https://github.com/bertugarangou/ExtrusoraPLA

  Circuit:
  - Extrusora feta per Albert Garangou,
    com a Treball de Recerca a 2n de Batxillerat,
    curs 2018/2019, tutor Jordi Fanals Oriol,
    codi amb Arduino IDE 1.8.5,

    Copyright (c) 2018 Albert Garangou Culebras (albertgarangou@gmail.com)
    This Font Software is licensed under the SIL Open Font License, Version 1.1.

*/
